# Fritzing sketch FunctionModule (saved by Fritzing 0.9.3b)
breadboards: 1

parts:
  Part1 = Arduino Uno (Rev3)
  R1 = Slide Potentiometer [maximum_resistance=100kΩ]
  R2 = Slide Potentiometer [maximum_resistance=100kΩ]
  R3 = Slide Potentiometer [maximum_resistance=100kΩ]

nets:
  N1: Part1.A0, R1.wiper
  N2: Part1.A1, R2.wiper
  N3: Part1.A2, R3.wiper
  N4: Part1.GND, R1.leg2, R2.leg2, R3.leg2
  N5: Part1.5V, R1.leg1, R2.leg1, R3.leg1
